# Fritzing sketch earthquake detector v1 (saved by Fritzing 0.9.3b)
circuit board: 10.0104cm x 7.65842cm
breadboards: 1

parts:
  Grove1 = Grove Buzz
  LED2 = LED - 5mm [color="Red (633nm)" package="5 mm [THT]"]
  LED3 = LED - 5mm [color="Red (633nm)" package="5 mm [THT]"]
  LED4 = LED - 5mm [color="Red (633nm)" package="5 mm [THT]"]
  R1 = Resistor [tolerance=±5% resistance=220 package="2512 [SMD]"]
  R2 = Resistor [tolerance=±5% resistance=220 package="2512 [SMD]"]
  R3 = Resistor [tolerance=±5% resistance=220 package="2512 [SMD]"]
  S1 = SPST Switch [package=switche-dpdt]
  C1 = Electrolytic Capacitor [capacitance=1µF package="100 mil [THT, electrolytic]"]
  R4 = Resistor [tolerance=±5% resistance=10k package="2512 [SMD]"]
  GY1 = MPU-6050 Board GY-521 [form="♀ (female)" package=THT]
  Part1 = Arduino Uno (Rev3) - ICSP

nets (from the pcb view):
  GND: Grove1.GND, R1.Pin_0, R2.Pin_0, R3.Pin_0, S1.O, R4.Pin_0, GY1.pin2, GY1.pin6, Part1.GND
  VCC: Grove1.VCC, S1.S, C1.+, GY1.pin1, Part1.5V
  N1: Grove1.SIG, Part1.D5_PWM
  N2: LED2.cathode, Part1.D9_PWM
  N3: LED2.anode, R1.Pin_1
  N4: LED3.cathode, Part1.D10_PWM/SS
  N5: LED3.anode, R2.Pin_1
  N6: LED4.cathode, Part1.D11_PWM/MOSI
  N7: LED4.anode, R3.Pin_1
  N8: S1.P, Part1.D4
  N9: C1.-, R4.Pin_1, Part1.D3_PWM
  N10: GY1.pin3, Part1.A5/SCL
  N11: GY1.pin4, Part1.A4/SDA
  N12: GY1.pin5, Part1.D2

notes:
  Adafruit Fast Vibration Switch (1766)

custom parts:
  MPU-6050 Board GY-521: Acelerometro y Giroscopio MPU-6050 Board GY-521
